# Fritzing sketch feeding_dust_display (saved by Fritzing 0.9.3b)
breadboards: 1

parts:
  Part1 = Arduino Pro Mini (5V)
  LCD2 = LCD screen
  LCM1602_IIC2 = LCM1602 IIC [part_number="LCM1602 IIC" chip_label="LCM1602 IIC" package="DIP (Dual Inline) [THT]"]
  U2 = XD-RF-5V
  LED2 = RGB LED - (4 legs) [package="5 mm [THT]"]
  IC1 = L293D [package=THT]
  M1 = DC Motor
  VCC1 = Battery

nets:
  N1: Part1.VCC, U2.connector0, IC1.Enable_1, IC1.+V
  N2: Part1.GND, U2.connector3, LED2.blue_cathode, IC1.0V, VCC1.-
  N3: Part1.A4, LCM1602_IIC2.SDA
  N4: Part1.A5, LCM1602_IIC2.SCL
  N5: Part1.MISO, LED2.green_cathode
  N6: Part1.MOSI, LED2.common_anode
  N7: Part1.D10, LED2.red_cathode
  N8: Part1.D5, IC1.In_2
  N9: Part1.D4, IC1.In_1
  N10: Part1.D2, U2.connector2
  VSS: LCD2.VSS, LCM1602_IIC2.VSS
  VDD: LCD2.VDD, LCM1602_IIC2.VDD
  N11: LCD2.V0, LCM1602_IIC2.V0
  N12: LCD2.RS, LCM1602_IIC2.RS
  N13: LCD2.R/W, LCM1602_IIC2.RW
  N14: LCD2.E, LCM1602_IIC2.E
  N15: LCD2.DB0, LCM1602_IIC2.D0
  N16: LCD2.DB1, LCM1602_IIC2.D1
  N17: LCD2.DB2, LCM1602_IIC2.D2
  N18: LCD2.DB3, LCM1602_IIC2.D3
  N19: LCD2.DB4, LCM1602_IIC2.D4
  N20: LCD2.DB5, LCM1602_IIC2.D5
  N21: LCD2.DB6, LCM1602_IIC2.D6
  N22: LCD2.DB7, LCM1602_IIC2.D7
  N23: LCD2.LED+, LCM1602_IIC2.A
  N24: LCD2.LED-, LCM1602_IIC2.K
  N25: LCM1602_IIC2.LED_A, LCM1602_IIC2.LED_B
  N26: IC1.Out_1_(_Controlled_by_Enable_1_), M1.pin_1
  N27: IC1.Out_2_(_Controlled_by_Enable_1_), M1.pin_2
  N28: IC1.+Vmotor, VCC1.+

custom parts:
  LCM1602 IIC: I2C-Module to use a 1602 or 2004 LCD on with the wire.h libory Serial LCD Modul
